# Fritzing sketch nano_01 (saved by Fritzing 1.0.3b)
breadboards: 1

parts:
  Part1 = Arduino Nano (Rev3.0) (ICSP)
  Part2 = NeoPixel Stick [part_number=1426]
  Part3 = NeoPixel Stick [part_number=1426]
  Part4 = 24 NeoPixel Ring [part_number=1586]
  R1 = Rotary Potentiometer (Large) [maximum_resistance=100kΩ knob_status=50% power=0.5W package=THT]
  R2 = Rotary Potentiometer (Large) [maximum_resistance=100kΩ knob_status=50% power=0.5W package=THT]

nets:
  GND: Part1.GND, Part2.GND, Part3.GND, Part4.GND, R1.leg2, R2.leg2
  N1: Part1.D6, Part2.DATAIN
  N2: Part1.D7, Part3.DATAIN
  N3: Part1.D8, Part4.IN
  +5V: Part1.5V, Part2.+5V, Part3.+5V, Part4.VDD, R1.leg1, R2.leg1
  N4: Part1.A1, R2.wiper
  N5: Part1.A0, R1.wiper

custom parts:
  NeoPixel Stick: Make your own little LED strip arrangement with this stick of NeoPixel LEDs. We crammed 8 of the tiny 5050 (5mm x 5mm) smart RGB LEDs onto a PCB with mounting holes and a chainable design. Use only one microcontroller pin to control as many as you can chain together! Each LED is addressable as the driver chip is inside the LED. Each one has ~18mA constant current drive so the color will be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
  24 NeoPixel Ring: 24 ultra bright smart LED NeoPixels are arranged in a circle with 2.6" (66mm) outer diameter. The rings are 'chainable' - connect the output pin of one to the input pin of another. Use only one microcontroller pin to control as many as you can chain together! Each LED is addressable as the driver chip is inside the LED. Each one has ~18mA constant current drive so the color will be very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
